// Logisim project Main.circ as structural Verilog: 2 circuits, main circuit main
module main (
);

  wire and_11_out, and_16_out, Cmd_01_1, Cmd_01_2, Cmd_02_1, Cmd_02_2, Cmd_03_1, Cmd_03_1_2_3, Cmd_03_2,
       Cmd_03_3, Cmd_03_4, Cmd_04_1, Cmd_04_1_2, Cmd_04_2, Cmd_04_3, Cmd_04_4, Cmd_05_1, Cmd_05_2, Cmd_06_1,
       Cmd_06_1_2, Cmd_06_2, Cmd_06_3, Cmd_06_4, CMD_START, LOAD_CMD, nor_1_out, nor_2_out, nor_3_out,
       nor_4_out, nor_6_out, nor_7_out, not_1_out, not_2_out, not_3_out, not_4_out, not_5_out, or_2_out,
       or_3_out, or_4_out, or_5_out, or_6_out, or_7_out, or_11_out, or_12_out, or_13_out, or_14_out,
       or_15_out, or_16_out, or_17_out, or_18_out, or_19_out, or_20_out, or_21_out, or_22_out, or_23_out,
       or_24_out, Read_A_1, Read_A_03, Read_B_1, Read_B_03, Read_C_1, Read_C_03, Read_D_1, Read_D_03, RESET,
       TICK, TICK_DELAY, Write_A_04, Write_B_04, Write_C_04, Write_D_04;
  wire [7:0] Address_X, CMD_BASE, CMD_ORDER, controlled_buffer_1_out, controlled_buffer_2_out,
       controlled_buffer_3_out, controlled_buffer_4_out, controlled_buffer_5_out, controlled_buffer_6_out,
       controlled_buffer_7_out, controlled_buffer_13_out, controlled_buffer_14_out, DATA, register_2_q,
       register_3_q, register_4_q, register_5_q, register_6_q, register_7_q;
  wire [15:0] ADDRESS, addressmassive_1_adr1, addressmassive_1_adr2, addressmassive_1_adr2_1,
       addressmassive_1_adr2_2, addressmassive_1_adr2_3, Adr1;

  Clock clock_1 (.out(TICK));
  Button button_1 (.out(RESET));
  // Probe on ADDRESS
  and and_1 (Cmd_01_1, nor_1_out, CMD_START, TICK_DELAY);
  // OR_Gate or_1 is placed but not wired
  or or_2 (or_2_out, ADDRESS[8], ADDRESS[9], ADDRESS[10], ADDRESS[11], ADDRESS[12], ADDRESS[13], ADDRESS[14], ADDRESS[15]);
  or or_3 (or_3_out, LOAD_CMD, Cmd_01_1, Cmd_03_1_2_3, Cmd_04_1_2, Cmd_05_1, Cmd_06_1_2);
  buf or_4 (or_4_out, Cmd_04_3);  // OR_Gate
  buf or_5 (or_5_out, LOAD_CMD);  // OR_Gate
  nor nor_1 (nor_1_out, ~CMD_BASE[2], CMD_BASE[3], CMD_BASE[4], CMD_BASE[5], CMD_BASE[6], CMD_BASE[7]);  // NOR_Gate
  and and_2 (Cmd_01_2, nor_1_out, ~TICK_DELAY, CMD_ORDER[7]);  // AND_Gate
  nor nor_2 (nor_2_out, CMD_BASE[2], ~CMD_BASE[3], CMD_BASE[4], CMD_BASE[5], CMD_BASE[6], CMD_BASE[7]);  // NOR_Gate
  and and_3 (Cmd_03_1, nor_2_out, CMD_START, TICK_DELAY);
  and and_4 (Cmd_03_2, nor_2_out, ~TICK_DELAY, CMD_ORDER[7]);  // AND_Gate
  and and_5 (Cmd_03_3, nor_2_out, TICK_DELAY, CMD_ORDER[7]);
  and and_6 (Cmd_03_4, nor_2_out, ~TICK_DELAY, CMD_ORDER[6]);  // AND_Gate
  nor nor_3 (nor_3_out, CMD_BASE[2], CMD_BASE[3], ~CMD_BASE[4], CMD_BASE[5], CMD_BASE[6], CMD_BASE[7]);  // NOR_Gate
  and and_7 (Cmd_06_1, nor_4_out, CMD_START, TICK_DELAY);
  and and_8 (Cmd_06_2, nor_4_out, ~TICK_DELAY, CMD_ORDER[7]);  // AND_Gate
  and and_9 (Cmd_06_3, nor_4_out, TICK_DELAY, CMD_ORDER[7]);
  and and_10 (Cmd_06_4, nor_4_out, ~TICK_DELAY, CMD_ORDER[6]);  // AND_Gate
  not not_1 (not_1_out, or_2_out);
  and and_11 (and_11_out, or_2_out, or_3_out);
  Shift_Register #(.trigger("falling")) shift_register_1 (
    .shift(1'b1), .in(CMD_START), .clk(TICK), .clr(or_6_out), .q0(CMD_ORDER[7]), .q1(CMD_ORDER[6]),
    .q2(CMD_ORDER[5]), .q3(CMD_ORDER[4]), .q4(CMD_ORDER[3]), .q5(CMD_ORDER[2]), .q6(CMD_ORDER[1]),
    .q7(CMD_ORDER[0]));  // open: out, load, d0, d1, d2, d3, d4, d5, d6, d7
  or or_6 (or_6_out, RESET, Cmd_01_2, Cmd_02_2, Cmd_03_4, Cmd_04_4, Cmd_05_2, Cmd_06_4);
  Register #(.trigger("high")) register_1 (
    .D(controlled_buffer_1_out), .Q(CMD_BASE), .clk(or_5_out), .clr(RESET));  // open: en
  assign controlled_buffer_1_out = or_5_out ? DATA : 8'bz;  // Controlled_Buffer controlled_buffer_1
  Demultiplexer #(.select(2)) demultiplexer_1 (
    .out0(Read_A_1), .out1(Read_B_1), .out2(Read_C_1), .out3(Read_D_1), .in(Cmd_01_1), .sel(CMD_BASE[1:0]),
    .en(1'b1));
  Demultiplexer #(.select(2)) demultiplexer_2 (
    .out0(Read_A_03), .out1(Read_B_03), .out2(Read_C_03), .out3(Read_D_03), .in(Cmd_03_3),
    .sel(CMD_BASE[1:0]), .en(1'b1));
  and and_12 (Cmd_04_1, nor_3_out, CMD_START, TICK_DELAY);
  and and_13 (Cmd_04_2, nor_3_out, ~TICK_DELAY, CMD_ORDER[7]);  // AND_Gate
  and and_14 (Cmd_04_3, nor_3_out, TICK_DELAY, CMD_ORDER[7]);
  and and_15 (Cmd_04_4, nor_3_out, ~TICK_DELAY, CMD_ORDER[6]);  // AND_Gate
  nor nor_4 (nor_4_out, CMD_BASE[0], ~CMD_BASE[1], CMD_BASE[2], CMD_BASE[3], CMD_BASE[4], CMD_BASE[5], CMD_BASE[6], CMD_BASE[7]);  // NOR_Gate
  and and_16 (and_16_out, not_1_out, or_3_out);
  or or_7 (or_7_out, and_11_out, or_4_out);
  not not_2 (not_2_out, or_4_out);
  Demultiplexer #(.select(2)) demultiplexer_3 (
    .out0(Write_A_04), .out1(Write_B_04), .out2(Write_C_04), .out3(Write_D_04), .in(Cmd_04_3),
    .sel(CMD_BASE[1:0]), .en(1'b1));
  nor nor_5 (CMD_START, CMD_ORDER[0], CMD_ORDER[1], CMD_ORDER[2], CMD_ORDER[3], CMD_ORDER[4], CMD_ORDER[5], CMD_ORDER[6], CMD_ORDER[7]);
  or or_8 (Cmd_03_1_2_3, Cmd_03_1, Cmd_03_2, Cmd_03_3);
  or or_9 (Cmd_04_1_2, Cmd_04_1, Cmd_04_2);
  or or_10 (Cmd_06_1_2, Cmd_06_1, Cmd_06_2);
  ROM rom_1 (.addr(ADDRESS[7:0]), .data(DATA), .sel(and_16_out));
  RAM #(.addrWidth(16), .bus("asynch")) ram_1 (
    .addr(ADDRESS), .data(DATA), .sel(or_7_out), .ld(not_2_out), .clr(RESET));
  // Probe on DATA
  not not_3 (not_3_out, TICK);
  and and_17 (LOAD_CMD, CMD_START, ~TICK_DELAY);  // AND_Gate
  not not_4 (not_4_out, not_3_out);
  not not_5 (not_5_out, not_4_out);
  assign controlled_buffer_2_out = or_11_out ? DATA : 8'bz;  // Controlled_Buffer controlled_buffer_2
  or or_11 (or_11_out, Cmd_03_1, Cmd_04_1, Cmd_05_1, Cmd_06_1);
  or or_12 (or_12_out, Cmd_03_2, Cmd_04_2, Cmd_06_2);
  or or_13 (or_13_out, Cmd_03_3, Cmd_04_3, Cmd_06_3);
  buf or_14 (or_14_out, Cmd_05_1);  // OR_Gate
  not not_6 (TICK_DELAY, not_5_out);
  nor nor_6 (nor_6_out, CMD_BASE[0], CMD_BASE[1], CMD_BASE[2], CMD_BASE[3], CMD_BASE[4], CMD_BASE[5], CMD_BASE[6], CMD_BASE[7]);
  Register #(.trigger("high")) register_2 (
    .D(controlled_buffer_2_out), .Q(register_2_q), .clk(or_11_out), .clr(RESET));  // open: en
  Register #(.trigger("high")) register_3 (
    .D(controlled_buffer_3_out), .Q(register_3_q), .clk(or_12_out), .clr(RESET));  // open: en
  assign controlled_buffer_3_out = or_12_out ? DATA : 8'bz;  // Controlled_Buffer controlled_buffer_3
  and and_18 (Cmd_05_1, nor_7_out, CMD_START, TICK_DELAY);
  or or_15 (or_15_out, Read_A_1, Read_A_03);
  buf or_16 (or_16_out, Write_A_04);  // OR_Gate
  or or_17 (or_17_out, Read_B_1, Read_B_03);
  buf or_18 (or_18_out, Write_B_04);  // OR_Gate
  assign controlled_buffer_4_out = or_13_out ? register_2_q : 8'bz;  // Controlled_Buffer controlled_buffer_4
  assign controlled_buffer_5_out = or_13_out ? register_3_q : 8'bz;  // Controlled_Buffer controlled_buffer_5
  nor nor_7 (nor_7_out, ~CMD_BASE[0], CMD_BASE[1], CMD_BASE[2], CMD_BASE[3], CMD_BASE[4], CMD_BASE[5], CMD_BASE[6], CMD_BASE[7]);  // NOR_Gate
  and and_19 (Cmd_05_2, nor_7_out, ~TICK_DELAY, CMD_ORDER[7]);  // AND_Gate
  assign controlled_buffer_6_out = or_15_out ? DATA : 8'bz;  // Controlled_Buffer controlled_buffer_6
  Register #(.trigger("high")) register_4 (
    .D(controlled_buffer_6_out), .Q(register_4_q), .clk(or_15_out), .clr(RESET));  // open: en
  assign controlled_buffer_7_out = or_17_out ? DATA : 8'bz;  // Controlled_Buffer controlled_buffer_7
  Register #(.trigger("high")) register_5 (
    .D(controlled_buffer_7_out), .Q(register_5_q), .clk(or_17_out), .clr(RESET));  // open: en
  and and_20 (Cmd_02_1, nor_6_out, CMD_START, TICK_DELAY);
  and and_21 (Cmd_02_2, nor_6_out, ~TICK_DELAY, CMD_ORDER[7]);  // AND_Gate
  assign Address_X = or_14_out ? register_2_q : 8'bz;  // Controlled_Buffer controlled_buffer_8
  assign DATA = or_16_out ? register_4_q : 8'bz;  // Controlled_Buffer controlled_buffer_9
  assign DATA = or_18_out ? register_5_q : 8'bz;  // Controlled_Buffer controlled_buffer_10
  assign Adr1 = or_20_out ? {controlled_buffer_5_out, controlled_buffer_4_out} : 16'bz;  // Controlled_Buffer controlled_buffer_11
  assign ADDRESS = or_19_out ? {controlled_buffer_5_out, controlled_buffer_4_out} : 16'bz;  // Controlled_Buffer controlled_buffer_12
  or or_19 (or_19_out, Cmd_03_3, Cmd_04_3);
  buf or_20 (or_20_out, Cmd_06_3);  // OR_Gate
  assign controlled_buffer_13_out = or_21_out ? DATA : 8'bz;  // Controlled_Buffer controlled_buffer_13
  or or_21 (or_21_out, Read_C_1, Read_C_03);
  buf or_22 (or_22_out, Write_C_04);  // OR_Gate
  assign controlled_buffer_14_out = or_23_out ? DATA : 8'bz;  // Controlled_Buffer controlled_buffer_14
  or or_23 (or_23_out, Read_D_1, Read_D_03);
  buf or_24 (or_24_out, Write_D_04);  // OR_Gate
  Register #(.trigger("high")) register_6 (
    .D(controlled_buffer_13_out), .Q(register_6_q), .clk(or_21_out), .clr(RESET));  // open: en
  assign DATA = or_22_out ? register_6_q : 8'bz;  // Controlled_Buffer controlled_buffer_15
  assign DATA = or_24_out ? register_7_q : 8'bz;  // Controlled_Buffer controlled_buffer_16
  Register #(.trigger("high")) register_7 (
    .D(controlled_buffer_14_out), .Q(register_7_q), .clk(or_23_out), .clr(RESET));  // open: en
  AddressMassive addressmassive_1 (
    .Adr_IN_01(Cmd_06_3), .Adr_IN_02(1'b0), .Adr_IN_03(1'b0), .Adr_IN_04(1'b0), .Adr_IN_05(1'b0),
    .Adr_IN_06(1'b0), .Adr_IN_07(1'b0), .Reset(RESET), .Adr_OUT_01(LOAD_CMD), .Adr_OUT_02(1'b0),
    .Adr_OUT_03(1'b0), .Adr_OUT_04(1'b0), .Adr_OUT_05(1'b0), .Adr_OUT_06(1'b0), .Adr_OUT_07(1'b0),
    .Copy_01(LOAD_CMD), .Copy_01_2(1'b0), .Copy_01_3(1'b0), .Copy_01_4(1'b0), .Copy_01_5(1'b0),
    .Copy_01_6(1'b0), .Copy_01_7(1'b0), .Adr___1_01(Cmd_01_1), .Adr___1_02(Cmd_03_1), .Adr___1_03(Cmd_04_1),
    .Adr___1_04(Cmd_05_1), .Adr___1_05(Cmd_06_1), .Adr___1_06(1'b0), .Adr___1_07(1'b0),
    .Adr___2_01(Cmd_03_2), .Adr___2_02(Cmd_04_2), .Adr___2_03(Cmd_06_2), .Adr___2_04(1'b0),
    .Adr___2_05(1'b0), .Adr___2_06(1'b0), .Adr___2_07(1'b0), .Adr___3_01(1'b0), .Adr___3_02(1'b0),
    .Adr___3_03(1'b0), .Adr___3_04(1'b0), .Adr___3_05(1'b0), .Adr___3_06(1'b0), .Adr___3_07(1'b0),
    .Address_OUT(ADDRESS), .Adr2_1(addressmassive_1_adr2_1), .Adr2_2(addressmassive_1_adr2_2),
    .Adr2_3(addressmassive_1_adr2_3), .Put___1_01(Cmd_02_1), .Put___1_02(1'b0), .Put___1_03(1'b0),
    .Put___1_04(1'b0), .Put___1_05(1'b0), .Put___1_06(1'b0), .Put___1_07(1'b0), .Put___2_01(Cmd_01_1),
    .Put___2_02(1'b0), .Put___2_03(1'b0), .Put___2_04(1'b0), .Put___2_05(1'b0), .Put___2_06(1'b0),
    .Put___2_07(1'b0), .Put___3_01(Cmd_03_3), .Put___3_02(Cmd_04_3), .Put___3_03(1'b0), .Put___3_04(1'b0),
    .Put___3_05(1'b0), .Put___3_06(1'b0), .Put___3_07(1'b0), .in_1(Adr1), .Adr1(addressmassive_1_adr1),
    .Adr2(addressmassive_1_adr2), .Put___X_01(Cmd_05_1), .Put___X_02(1'b0), .Put___X_03(1'b0),
    .Put___X_04(1'b0), .Put___X_05(1'b0), .Put___X_06(1'b0), .Put___X_07(1'b0), .X(Address_X));
  // Probe on addressmassive_1_adr1
  // Probe on addressmassive_1_adr2
  // Probe on addressmassive_1_adr2_1
  // Probe on addressmassive_1_adr2_2
  // Probe on addressmassive_1_adr2_3
  // Probe on ADDRESS

  // Notes on the sheet:
  //   CMD 03: LET     [Const]  ---> R
  //   CMD 04: LET     R  --->  [Const16]
  //   CMD 06: JMP     [Const16]  ---> A
  //   CMD 01: LET     Const  ---> R
  //   Register CMD
  //   contents of rom_1 (hex, n*v repeats v):
  //   2 c 6*0 1 f8 0 0 2 8 194*0 13 0 0 0 66 0 0 0 34 0 0 0 12
  //   CMD_MAIN_LOGIC
  //   CMD 02: No Op
  //   Register X1
  //   Register X2
  //   CMD 05: JMP     A + Const8
  //   Register A (00)
  //   Register B (01)
  //   Register C (10)
  //   Register D (11)
endmodule

module AddressMassive (
  input  [15:0] in_1,
  input  Adr_IN_01,
  input  Adr_IN_02,
  input  Adr_IN_03,
  input  Adr_IN_04,
  input  Adr_IN_05,
  input  Adr_IN_06,
  input  Adr_IN_07,
  input  Reset,
  input  Adr_OUT_01,
  input  Adr_OUT_02,
  input  Adr_OUT_03,
  input  Adr_OUT_04,
  input  Adr_OUT_05,
  input  Adr_OUT_06,
  input  Adr_OUT_07,
  input  Copy_01,
  input  Copy_01_2,
  input  Copy_01_3,
  input  Copy_01_4,
  input  Copy_01_5,
  input  Copy_01_6,
  input  Copy_01_7,
  input  Adr___1_01,
  input  Adr___1_02,
  input  Adr___1_03,
  input  Adr___1_04,
  input  Adr___1_05,
  input  Adr___1_06,
  input  Adr___1_07,
  input  Adr___2_01,
  input  Adr___2_02,
  input  Adr___2_03,
  input  Adr___2_04,
  input  Adr___2_05,
  input  Adr___2_06,
  input  Adr___2_07,
  input  Adr___3_01,
  input  Adr___3_02,
  input  Adr___3_03,
  input  Adr___3_04,
  input  Adr___3_05,
  input  Adr___3_06,
  input  Adr___3_07,
  input  Put___1_01,
  input  Put___1_02,
  input  Put___1_03,
  input  Put___1_04,
  input  Put___1_05,
  input  Put___1_06,
  input  Put___1_07,
  input  Put___2_01,
  input  Put___2_02,
  input  Put___2_03,
  input  Put___2_04,
  input  Put___2_05,
  input  Put___2_06,
  input  Put___2_07,
  input  Put___3_01,
  input  Put___3_02,
  input  Put___3_03,
  input  Put___3_04,
  input  Put___3_05,
  input  Put___3_06,
  input  Put___3_07,
  input  [7:0] X,
  input  Put___X_01,
  input  Put___X_02,
  input  Put___X_03,
  input  Put___X_04,
  input  Put___X_05,
  input  Put___X_06,
  input  Put___X_07,
  output [15:0] Address_OUT,
  output [15:0] Adr1,
  output [15:0] Adr2,
  output [15:0] Adr2_1,
  output [15:0] Adr2_2,
  output [15:0] Adr2_3
);

  wire or_1_out, or_2_out, or_3_out, or_4_out, or_5_out, or_6_out, or_7_out, or_8_out, or_9_out, or_10_out,
       or_11_out;
  wire [15:0] adder_4_out, controlled_buffer_1_out, controlled_buffer_2_out;

  or or_1 (or_1_out, Adr_IN_01, Adr_IN_02, Adr_IN_03, Adr_IN_04, Adr_IN_05, Adr_IN_06, Adr_IN_07);
  or or_2 (or_2_out, Adr_OUT_01, Adr_OUT_02, Adr_OUT_03, Adr_OUT_04, Adr_OUT_05, Adr_OUT_06, Adr_OUT_07);
  or or_3 (or_3_out, Copy_01, Copy_01_2, Copy_01_3, Copy_01_4, Copy_01_5, Copy_01_6, Copy_01_7);
  or or_4 (or_4_out, Adr___1_01, Adr___1_02, Adr___1_03, Adr___1_04, Adr___1_05, Adr___1_06, Adr___1_07);
  or or_5 (or_5_out, Adr___2_01, Adr___2_02, Adr___2_03, Adr___2_04, Adr___2_05, Adr___2_06, Adr___2_07);
  or or_6 (or_6_out, Adr___3_01, Adr___3_02, Adr___3_03, Adr___3_04, Adr___3_05, Adr___3_06, Adr___3_07);
  or or_7 (or_7_out, Put___1_01, Put___1_02, Put___1_03, Put___1_04, Put___1_05, Put___1_06, Put___1_07);
  or or_8 (or_8_out, Put___2_01, Put___2_02, Put___2_03, Put___2_04, Put___2_05, Put___2_06, Put___2_07);
  or or_9 (or_9_out, Put___3_01, Put___3_02, Put___3_03, Put___3_04, Put___3_05, Put___3_06, Put___3_07);
  or or_10 (or_10_out, Put___X_01, Put___X_02, Put___X_03, Put___X_04, Put___X_05, Put___X_06, Put___X_07);
  assign controlled_buffer_1_out = or_1_out ? in_1 : 16'bz;  // Controlled_Buffer controlled_buffer_1
  or or_11 (or_11_out, or_1_out, or_7_out, or_8_out, or_9_out, or_10_out);
  Register #(.width(16), .trigger("high")) register_1 (
    .D(controlled_buffer_1_out), .Q(Adr1), .clk(or_11_out), .clr(Reset));  // open: en
  Register #(.width(16), .trigger("high")) register_2 (
    .D(controlled_buffer_2_out), .Q(Adr2), .clk(or_3_out), .clr(Reset));  // open: en
  assign controlled_buffer_2_out = or_3_out ? Adr1 : 16'bz;  // Controlled_Buffer controlled_buffer_2
  assign Address_OUT = or_2_out ? Adr1 : 16'bz;  // Controlled_Buffer controlled_buffer_3
  assign controlled_buffer_1_out = or_7_out ? Adr2_1 : 16'bz;  // Controlled_Buffer controlled_buffer_4
  assign controlled_buffer_1_out = or_8_out ? Adr2_2 : 16'bz;  // Controlled_Buffer controlled_buffer_5
  assign controlled_buffer_1_out = or_9_out ? Adr2_3 : 16'bz;  // Controlled_Buffer controlled_buffer_6
  Adder #(.width(16)) adder_1 (.a(Adr2), .b(16'h1), .out(Adr2_1), .cin(1'b0));  // open: cout
  Adder #(.width(16)) adder_2 (.a(Adr2), .b(16'h2), .out(Adr2_2), .cin(1'b0));  // open: cout
  Adder #(.width(16)) adder_3 (.a(Adr2), .b(16'h3), .out(Adr2_3), .cin(1'b0));  // open: cout
  Adder #(.width(16)) adder_4 (.a(Adr2), .b({{9{X[7]}}, X[6:0]}), .out(adder_4_out), .cin(1'b0));  // open: cout
  assign controlled_buffer_1_out = or_10_out ? adder_4_out : 16'bz;  // Controlled_Buffer controlled_buffer_7
  assign Address_OUT = or_4_out ? Adr2_1 : 16'bz;  // Controlled_Buffer controlled_buffer_8
  assign Address_OUT = or_5_out ? Adr2_2 : 16'bz;  // Controlled_Buffer controlled_buffer_9
  assign Address_OUT = or_6_out ? Adr2_3 : 16'bz;  // Controlled_Buffer controlled_buffer_10
endmodule
